// Logisim project calculator.circ as structural Verilog
module main (
);

  wire w0, w1, w2, w3, w4, w5, w6, w7, w8, w9;
  wire [15:0] QAReg, shifter_1_out;

  Register #(.width(4)) register_1 ();  // open: D, en, Q, clk, clr
  Button button_1 (.out(w7));
  Button button_2 (.out(w4));
  Button button_3 (.out(w1));
  Button button_4 (.out(w0));
  Register #(.width(4)) register_2 ();  // open: D, en, Q, clk, clr
  Button button_5 (.out(w8));
  Button button_6 (.out(w5));
  Button button_7 (.out(w2));
  Button button_8 (.out(w9));
  Button button_9 (.out(w6));
  Button button_10 (.out(w3));
  Register #(.width(4)) register_3 ();  // open: D, en, Q, clk, clr
  Register #(.width(4)) register_4 ();  // open: D, en, Q, clk, clr
  Shifter #(.width(16)) shifter_1 (.in(QAReg), .\dist (4'b0001), .out(shifter_1_out));
  Register #(.width(16)) register_5 (.Q(QAReg));  // open: D, en, clk, clr
  Register #(.width(4)) register_6 ();  // open: D, en, Q, clk, clr
  Adder #(.width(16)) adder_1 (.a(shifter_1_out));  // open: b, out, cin, cout
endmodule

module Mult (
  input  [15:0] A,
  input  [15:0] B,
  input  start,
  input  clk,
  output [15:0] S
);

  wire [15:0] add_result, multiplexer_1_out, multiplicand, product;
  wire [31:0] multiplexer_2_out;

  // Probe on A
  // Probe on B
  // Probe on S
  Register #(.width(16)) u_Multiplicand (.D(A), .en(start), .clk(start), .Q(multiplicand));  // open: clr
  Multiplexer #(.width(16), .enable("false")) multiplexer_1 (
    .in0(product), .in1(add_result), .out(multiplexer_1_out), .sel(S[0]));
  Multiplexer #(.width(32), .enable("false")) multiplexer_2 (
    .in0({1'b0, multiplexer_1_out, S[15:1]}), .in1({{16{1'b0}}, B}), .out(multiplexer_2_out), .sel(start));
  Register #(.width(32)) ProductMultipler (.D(multiplexer_2_out), .en(1'b1), .clk(clk), .Q({product, S}));  // open: clr
  Adder #(.width(16)) adder_1 (.a(product), .b(multiplicand), .out(add_result));  // open: cin, cout

  // Other names for the same wires on the sheet: multiplier[15:0] = S; lsb = S[0]; strt = start
endmodule

module Ad (
  input  Sub,
  input  [15:0] A,
  input  [15:0] B,
  output [15:0] out_4
);

  wire adder_1_cout, adder_2_cout, adder_3_cout;

  Adder #(.width(4)) adder_1 (.a(A[3:0]), .b(B[3:0]), .out(out_4[3:0]), .cin(Sub), .cout(adder_1_cout));
  Adder #(.width(4)) adder_2 (.a(A[7:4]), .b(B[7:4]), .out(out_4[7:4]), .cin(adder_1_cout), .cout(adder_2_cout));
  Adder #(.width(4)) adder_3 (.a(A[11:8]), .b(B[11:8]), .out(out_4[11:8]), .cin(adder_2_cout), .cout(adder_3_cout));
  Adder #(.width(4)) adder_4 (.a(A[15:12]), .b(B[15:12]), .out(out_4[15:12]), .cin(adder_3_cout));  // open: cout

  // Other names for the same wires on the sheet: a0[3:0] = A[3:0]; a1[3:0] = A[7:4]; a2[3:0] = A[11:8];
  //   a3[3:0] = A[15:12]; b0[3:0] = B[3:0]; b1[3:0] = B[7:4]; b2[3:0] = B[11:8]; b3[3:0] = B[15:12];
  //   s0[3:0] = out_4[3:0]; s1[3:0] = out_4[7:4]; s2[3:0] = out_4[11:8]; s3[3:0] = out_4[15:12]
endmodule
